// Logisim project morse2serial.circ as structural Verilog: 6 circuits, main circuit main
module main (
);

  wire buffer_1_out, buffer_2_out, buffer_3_out, buffer_4_out, buffer_5_out, button_1_out, button_2_out,
       char_received, clk1, clk2, clk4, clk8, counter_2_carry, data,
       eprom_morse_transmitter_1_load_next_char, keyboard_1_avail, morse, not_1_out, not_2_out, or_1_out,
       or_3_out, por_1_out, reset_state, rst, rst_out, serial, t_ff_1_q, uart_receiver_1_data_ready,
       uart_receiver_1_framing_error, uart_receiver_1_parity_error, word_received;
  wire [5:0] code, multiplexer_1_out;
  wire [6:0] keyboard_1_data, shift_register_1_out, shift_register_1_q0, shift_register_1_q1,
       shift_register_1_q2, shift_register_1_q3, shift_register_1_q4, shift_register_1_q5,
       shift_register_1_q6, shift_register_1_q7, shift_register_1_q8, shift_register_1_q9,
       shift_register_1_q10, shift_register_1_q11, shift_register_1_q12, shift_register_1_q13,
       shift_register_1_q14, shift_register_1_q15, shift_register_1_q16, shift_register_1_q17,
       shift_register_1_q18, shift_register_1_q19, shift_register_1_q20, shift_register_1_q21,
       shift_register_1_q22, shift_register_1_q23, shift_register_1_q24, shift_register_1_q25,
       shift_register_1_q26, shift_register_1_q27, shift_register_1_q28, shift_register_1_q29,
       shift_register_1_q30, shift_register_1_q31, shift_register_1_q32, shift_register_1_q33,
       shift_register_1_q34, shift_register_1_q35, shift_register_1_q36, shift_register_1_q37,
       shift_register_1_q38, shift_register_1_q39, shift_register_1_q40, shift_register_1_q41,
       shift_register_1_q42, shift_register_1_q43, shift_register_1_q44, shift_register_1_q45,
       shift_register_1_q46, shift_register_1_q47, shift_register_1_q48, shift_register_1_q49,
       shift_register_1_q50, shift_register_1_q51, shift_register_1_q52, shift_register_1_q53,
       shift_register_1_q54, shift_register_1_q55, shift_register_1_q56, shift_register_1_q57,
       shift_register_1_q58, shift_register_1_q59, shift_register_1_q60, shift_register_1_q61,
       shift_register_1_q62;
  wire [6:6] pull_resistor_1_node, t_ff_2_q;
  wire [7:0] morse_statemachine_data, uart_receiver_1_data_out, UART_STATE_MACHINE_data;
  wire [7:7] pull_resistor_1_node_2;
  wire [8:4] counter_1_q;

  Keyboard keyboard_1 (
    .clk(eprom_morse_transmitter_1_load_next_char), .clr(or_1_out), .avail(keyboard_1_avail),
    .data(keyboard_1_data));  // open: re
  or or_1 (or_1_out, button_1_out, rst);
  Button button_1 (.out(button_1_out));
  Counter counter_1 (.Q({counter_1_q, clk8, clk4, clk2}), .clk(clk1));  // open: load, D, count, carry, up, clr
  Clock clock_1 (.out(clk1));
  Counter #(.max('h5), .ongoal("stay"), .width(3)) counter_2 (
    .carry(counter_2_carry), .clk(clk8), .clr(not_1_out));  // open: load, D, count, Q, up
  not not_1 (not_1_out, morse);
  ROM #(.addrWidth(10)) morse_statemachine (
    .addr({reset_state, data, morse, pull_resistor_1_node[6], code}), .data(morse_statemachine_data));
  // Probe on {pull_resistor_1_node[6], code}
  POR por_1 (.out(por_1_out));
  Button u_rst (.out(rst_out));
  buf buffer_1 (buffer_1_out, counter_2_carry);
  buf buffer_2 (buffer_2_out, buffer_1_out);
  buf buffer_3 (buffer_3_out, buffer_2_out);
  buf buffer_4 (buffer_4_out, buffer_3_out);
  // Probe on {reset_state, data, morse, pull_resistor_1_node[6], code}
  Shift_Register #(.length(64), .width(7)) shift_register_1 (
    .in({morse, data, char_received, word_received, serial, reset_state, clk4}), .clk(clk2),
    .out(shift_register_1_out), .q0(shift_register_1_q0), .q1(shift_register_1_q1), .q2(shift_register_1_q2),
    .q3(shift_register_1_q3), .q4(shift_register_1_q4), .q5(shift_register_1_q5), .q6(shift_register_1_q6),
    .q7(shift_register_1_q7), .q8(shift_register_1_q8), .q9(shift_register_1_q9), .q10(shift_register_1_q10),
    .q11(shift_register_1_q11), .q12(shift_register_1_q12), .q13(shift_register_1_q13),
    .q14(shift_register_1_q14), .q15(shift_register_1_q15), .q16(shift_register_1_q16),
    .q17(shift_register_1_q17), .q18(shift_register_1_q18), .q19(shift_register_1_q19),
    .q20(shift_register_1_q20), .q21(shift_register_1_q21), .q22(shift_register_1_q22),
    .q23(shift_register_1_q23), .q24(shift_register_1_q24), .q25(shift_register_1_q25),
    .q26(shift_register_1_q26), .q27(shift_register_1_q27), .q28(shift_register_1_q28),
    .q29(shift_register_1_q29), .q30(shift_register_1_q30), .q31(shift_register_1_q31),
    .q32(shift_register_1_q32), .q33(shift_register_1_q33), .q34(shift_register_1_q34),
    .q35(shift_register_1_q35), .q36(shift_register_1_q36), .q37(shift_register_1_q37),
    .q38(shift_register_1_q38), .q39(shift_register_1_q39), .q40(shift_register_1_q40),
    .q41(shift_register_1_q41), .q42(shift_register_1_q42), .q43(shift_register_1_q43),
    .q44(shift_register_1_q44), .q45(shift_register_1_q45), .q46(shift_register_1_q46),
    .q47(shift_register_1_q47), .q48(shift_register_1_q48), .q49(shift_register_1_q49),
    .q50(shift_register_1_q50), .q51(shift_register_1_q51), .q52(shift_register_1_q52),
    .q53(shift_register_1_q53), .q54(shift_register_1_q54), .q55(shift_register_1_q55),
    .q56(shift_register_1_q56), .q57(shift_register_1_q57), .q58(shift_register_1_q58),
    .q59(shift_register_1_q59), .q60(shift_register_1_q60), .q61(shift_register_1_q61),
    .q62(shift_register_1_q62), .q63(shift_register_1_out));  // open: shift, load, clr, d0, d1, d2, d3, d4, d5, d6, d7, d8, d9, d10, d11, d12, d13, d14, d15, d16, d17, d18, d19, d20, d21, d22, d23, d24, d25, d26, d27, d28, d29, d30, d31, d32, d33, d34, d35, d36, d37, d38, d39, d40, d41, d42, d43, d44, d45, d46, d47, d48, d49, d50, d51, d52, d53, d54, d55, d56, d57, d58, d59, d60, d61, d62, d63
  DotMatrix #(.matrixcols(64)) dotmatrix_1 (
    .col0(shift_register_1_q0), .col1(shift_register_1_q1), .col2(shift_register_1_q2),
    .col3(shift_register_1_q3), .col4(shift_register_1_q4), .col5(shift_register_1_q5),
    .col6(shift_register_1_q6), .col7(shift_register_1_q7), .col8(shift_register_1_q8),
    .col9(shift_register_1_q9), .col10(shift_register_1_q10), .col11(shift_register_1_q11),
    .col12(shift_register_1_q12), .col13(shift_register_1_q13), .col14(shift_register_1_q14),
    .col15(shift_register_1_q15), .col16(shift_register_1_q16), .col17(shift_register_1_q17),
    .col18(shift_register_1_q18), .col19(shift_register_1_q19), .col20(shift_register_1_q20),
    .col21(shift_register_1_q21), .col22(shift_register_1_q22), .col23(shift_register_1_q23),
    .col24(shift_register_1_q24), .col25(shift_register_1_q25), .col26(shift_register_1_q26),
    .col27(shift_register_1_q27), .col28(shift_register_1_q28), .col29(shift_register_1_q29),
    .col30(shift_register_1_q30), .col31(shift_register_1_q31), .col32(shift_register_1_q32),
    .col33(shift_register_1_q33), .col34(shift_register_1_q34), .col35(shift_register_1_q35),
    .col36(shift_register_1_q36), .col37(shift_register_1_q37), .col38(shift_register_1_q38),
    .col39(shift_register_1_q39), .col40(shift_register_1_q40), .col41(shift_register_1_q41),
    .col42(shift_register_1_q42), .col43(shift_register_1_q43), .col44(shift_register_1_q44),
    .col45(shift_register_1_q45), .col46(shift_register_1_q46), .col47(shift_register_1_q47),
    .col48(shift_register_1_q48), .col49(shift_register_1_q49), .col50(shift_register_1_q50),
    .col51(shift_register_1_q51), .col52(shift_register_1_q52), .col53(shift_register_1_q53),
    .col54(shift_register_1_q54), .col55(shift_register_1_q55), .col56(shift_register_1_q56),
    .col57(shift_register_1_q57), .col58(shift_register_1_q58), .col59(shift_register_1_q59),
    .col60(shift_register_1_q60), .col61(shift_register_1_q61), .col62(shift_register_1_q62),
    .col63(shift_register_1_out));
  or or_2 (rst, por_1_out, rst_out);
  buf buffer_5 (buffer_5_out, buffer_4_out);
  buf buffer_6 (data, buffer_5_out);
  not not_2 (not_2_out, rst);
  EPROM_morse_transmitter eprom_morse_transmitter_1 (
    .clk(clk8), .char_available(keyboard_1_avail), .parallel_in({1'b0, keyboard_1_data}), .rst(rst),
    .load_next_char(eprom_morse_transmitter_1_load_next_char), .serial_out(morse));
  Pull_Resistor pull_resistor_1 (.node({pull_resistor_1_node_2[7], pull_resistor_1_node[6], code}));
  assign {pull_resistor_1_node_2[7], pull_resistor_1_node[6], code} = not_2_out ? morse_statemachine_data : 8'bz;  // Controlled_Buffer controlled_buffer_1
  Counter #(.max('h6), .ongoal("stay"), .width(3)) counter_3 (
    .load(rst), .D(3'b110), .carry(char_received), .clk(clk8), .clr(morse));  // open: count, Q, up
  // Probe on {code, word_received, char_received, t_ff_2_q[6], multiplexer_1_out}
  T_Flip_Flop t_ff_1 (.clk(clk1), .T(1'b1), .Q(t_ff_1_q));  // open: Qn, preset, reset
  T_Flip_Flop t_ff_2 (.clk(t_ff_1_q), .T(1'b1), .Q(t_ff_2_q[6]));  // open: Qn, preset, reset
  // Probe on multiplexer_1_out
  ROM #(.addrWidth(15)) UART_STATE_MACHINE (
    .addr({code, word_received, char_received, t_ff_2_q[6], multiplexer_1_out}),
    .data(UART_STATE_MACHINE_data));
  uart_receiver uart_receiver_1 (
    .rst(rst), .clk(clk1), .serial_in(serial), .data_out(uart_receiver_1_data_out),
    .data_ready(uart_receiver_1_data_ready), .framing_error(uart_receiver_1_framing_error),
    .parity_error(uart_receiver_1_parity_error));
  LED led_1 (.in(uart_receiver_1_framing_error));
  LED led_2 (.in(uart_receiver_1_parity_error));
  Counter #(.max('hf), .ongoal("stay"), .width(4)) counter_4 (
    .load(rst), .D(4'b1111), .carry(word_received), .clk(clk8), .clr(morse));  // open: count, Q, up
  TTY tty_1 (.data(uart_receiver_1_data_out[6:0]), .clk(uart_receiver_1_data_ready), .clr(or_3_out));  // open: we
  or or_3 (or_3_out, button_2_out, rst);
  Button button_2 (.out(button_2_out));
  Multiplexer #(.enable("false"), .width(8)) multiplexer_1 (
    .in0(UART_STATE_MACHINE_data), .in1(8'h60), .out({reset_state, serial, multiplexer_1_out}), .sel(rst));

  // Other names for the same wires on the sheet: sclk = clk1; mclk = clk8

  // Notes on the sheet:
  //   contents of morse_statemachine (hex, n*v repeats v):
  //   0 a1 83 83 c4 85 86 a7 98 89 8a 8f 8c ad ce 8f 92 91 92 d3 94 91 d6 97 98 d9 da 9b 9d 9d 9e df b0 a1
  //   a2 e3 a4 85 e6 a7 a8 e9 ae ab ec ad ae ef b0 f1 ba b3 f4 b5 b6 f7 f8 b9 ba fb bc b9 bf bf c1 c1 c2
  //   cb c4 c4 86 c7 c8 c8 8a cb 8c cd ce df d0 91 92 d3 94 d5 d6 d6 d9 d9 da da dc 9d 9e df e0 e0 ea e3
  //   a4 e5 e6 a7 e9 e9 ea ab ec ad ef ef f1 f1 f2 f7 f4 d5 b6 f7 f8 b9 fe fb bc fd fe bf c0 81 82 c3 84
  //   c5 c6 87 88 c9 ca 8b cc 8d 8e cf 90 d1 d2 93 d4 95 96 d7 d8 99 9a db 9c dd de 9f a0 e1 e2 a3 e4 a5
  //   a6 e7 e8 a9 aa eb ac ed ee af f0 b1 b2 f3 b4 f5 f6 b7 b8 f9 fa bb fc bd be ff c0 81 82 c3 84 c5 c6
  //   87 88 c9 ca 8b cc 8d 8e cf 90 d1 d2 93 d4 95 96 d7 d8 99 9a db 9c dd de 9f a0 e1 e2 a3 e4 a5 a6 e7
  //   e8 a9 aa eb ac ed ee af f0 b1 b2 f3 b4 f5 f6 b7 b8 f9 fa bb fc bd be ff 0 89 a2 83 c4 85 86 97 a8 89
  //   8a 9b 8c 8c ce 8f d0 91 92 d3 94 94 86 97 98 d9 da 9b dc 9d 9e 9e a4 a1 a2 e3 a4 b5 e6 a7 a8 ab 8a
  //   ab bc ad ae ef b0 f1 b3 b3 f4 b5 b6 f7 f8 b9 ba fb bc fd b6 bf c2 c1 c2 c7 c4 85 86 c7 c8 cd 8a cb
  //   dc cd ce ce d0 91 92 d3 94 d5 d6 97 d0 d9 da d3 dc 9d 9e df e0 e5 f2 e3 e6 e5 e6 e3 a8 e9 ea ab ec
  //   fd ec ef f8 f1 f2 fb f4 f4 b6 f7 f8 b9 ba fb bc fd fe bf c0 81 82 c3 84 c5 c6 87 88 c9 ca 8b cc 8d
  //   8e cf 90 d1 d2 93 d4 95 96 d7 d8 99 9a db 9c dd de 9f a0 e1 e2 a3 e4 a5 a6 e7 e8 a9 aa eb ac ed ee
  //   af f0 b1 b2 f3 b4 f5 f6 b7 b8 f9 fa bb fc bd be ff c0 81 82 c3 84 c5 c6 87 88 c9 ca 8b cc 8d 8e cf
  //   90 d1 d2 93 d4 95 96 d7 d8 99 9a db 9c dd de 9f a0 e1 e2 a3 e4 a5 a6 e7 e8 a9 aa eb ac ed ee af f0
  //   b1 b2 f3 b4 f5 f6 b7 b8 f9 fa bb fc bd be ff 0 0 0 82 85 a5 96 83 89 81 aa 83 8d 89 8f 8b 98 95 90
  //   9b 95 b5 97 87 88 98 9b 8b 8c 9c 9f 8f a1 81 82 a7 a0 a1 a4 87 88 a8 a2 a9 ae 8d aa ae a0 b0 a2 b2
  //   b5 a5 be b3 b0 bd b2 b3 ac ad ba be 0 1 2 3 4 5 6 7 8 9 a b c d e f 10 11 12 13 14 15 16 17 18 19 1a
  //   1b 1c 1d 1e 1f 20 21 22 23 24 25 26 27 28 29 2a 2b 2c 2d 2e 2f 30 31 32 33 34 35 36 37 38 39 3a 3b
  //   3c 3d 3e 3f 80 80 80 82 85 a5 96 83 89 81 aa 83 8d 89 8f 8b 98 95 90 9b 95 b5 97 87 88 98 9b 8b 8c
  //   9c 9f 8f a1 81 82 a7 a0 a1 a4 87 88 a8 a2 a9 ae 8d aa ae a0 b0 a2 b2 b5 a5 be b3 b0 bd b2 b3 ac ad
  //   ba be 0 1 2 3 4 5 6 7 8 9 a b c d e f 10 11 12 13 14 15 16 17 18 19 1a 1b 1c 1d 1e 1f 20 21 22 23 24
  //   25 26 27 28 29 2a 2b 2c 2d 2e 2f 30 31 32 33 34 35 36 37 38 39 3a 3b 3c 3d 3e 3f 80 80 80 82 85 a5
  //   96 83 89 81 aa 83 8d 89 8f 8b 98 95 90 9b 95 b5 97 87 88 98 9b 8b 8c 9c 9f 8f a1 81 82 a7 a0 a1 a4
  //   87 88 a8 a2 a9 ae 8d aa ae a0 b0 a2 b2 b5 a5 be b3 b0 bd b2 b3 ac ad ba be 0 1 2 3 4 5 6 7 8 9 a b c
  //   d e f 10 11 12 13 14 15 16 17 18 19 1a 1b 1c 1d 1e 1f 20 21 22 23 24 25 26 27 28 29 2a 2b 2c 2d 2e
  //   2f 30 31 32 33 34 35 36 37 38 39 3a 3b 3c 3d 3e 3f 80 80 80 82 85 a5 96 83 89 81 aa 83 8d 89 8f 8b
  //   98 95 90 9b 95 b5 97 87 88 98 9b 8b 8c 9c 9f 8f a1 81 82 a7 a0 a1 a4 87 88 a8 a2 a9 ae 8d aa ae a0
  //   b0 a2 b2 b5 a5 be b3 b0 bd b2 b3 ac ad ba be 0 1 2 3 4 5 6 7 8 9 a b c d e f 10 11 12 13 14 15 16 17
  //   18 19 1a 1b 1c 1d 1e 1f 20 21 22 23 24 25 26 27 28 29 2a 2b 2c 2d 2e 2f 30 31 32 33 34 35 36 37 38
  //   39 3a 3b 3c 3d 3e 3f
  //   contents of UART_STATE_MACHINE (hex, n*v repeats v):
  //   40 41 6 7 4 4 7 7 8 8 b b d d a b d0 d0 13 13 15 15 12 13 19 19 1e 5f 1c 1c 1f 5f 60 60 23 23 25 25
  //   22 23 29 29 2e 6f 2c 2c 2f 6f 71 71 36 37 34 34 37 37 38 38 3b 3b 3d 3d 3a 3b 40 3 6 3 c 5 7 5 18 9
  //   b 9 c f a f 40 d1 13 d1 14 17 12 17 18 5b 1e 5b 14 1d 1f 1d 40 61 23 61 24 27 22 27 28 6b 2e 6b 24
  //   2d 2f 2d 70 33 36 33 3c 35 37 35 28 39 3b 39 3c 3f 3a 3f 41 41 6 7 4 4 7 7 8 8 b b d d a b d0 d0 13
  //   13 15 15 12 13 19 19 1e 5f 1c 1c 1f 5f 60 60 23 23 25 25 22 23 29 29 2e 6f 2c 2c 2f 6f 71 71 36 37
  //   34 34 37 37 38 38 3b 3b 3d 3d 3a 3b 40 3 6 3 c 5 7 5 18 9 b 9 c f a f d0 d1 13 d1 14 17 12 17 18 5b
  //   1e 5b 14 1d 1f 1d 60 61 23 61 24 27 22 27 28 6b 2e 6b 24 2d 2f 2d 70 33 36 33 3c 35 37 35 28 39 3b
  //   39 3c 3f 3a 3f 40 41 6 7 4 4 7 7 8 8 b b d d a b d0 d0 13 13 15 15 12 13 19 19 1e 5f 1c 1c 1f 5f 60
  //   60 23 23 25 25 22 23 29 29 2e 6f 2c 2c 2f 6f 71 71 36 37 34 34 37 37 38 38 3b 3b 3d 3d 3a 3b 40 3 6
  //   3 c 5 7 5 18 9 b 9 c f a f 40 d1 13 d1 14 17 12 17 18 5b 1e 5b 14 1d 1f 1d 40 61 23 61 24 27 22 27
  //   28 6b 2e 6b 24 2d 2f 2d 70 33 36 33 3c 35 37 35 28 39 3b 39 3c 3f 3a 3f 41 41 6 7 4 4 7 7 8 8 b b d
  //   d a b d0 d0 13 13 15 15 12 13 19 19 1e 5f 1c 1c 1f 5f 60 60 23 23 25 25 22 23 29 29 2e 6f 2c 2c 2f
  //   6f 71 71 36 37 34 34 37 37 38 38 3b 3b 3d 3d 3a 3b 40 3 6 3 c 5 7 5 18 9 b 9 c f a f 70 d1 13 d1 14
  //   17 12 17 18 5b 1e 5b 14 1d 1f 1d 60 61 23 61 24 27 22 27 28 6b 2e 6b 24 2d 2f 2d 70 33 36 33 3c 35
  //   37 35 28 39 3b 39 3c 3f 3a 3f 40 41 6 7 44 44 7 7 8 8 b 4b d d a 4b d0 d0 13 53 15 15 12 53 19 19 1e
  //   5f 5c 5c 1f 5f 60 60 23 23 25 25 22 23 29 29 2e 6f 2c 2c 2f 6f 71 71 36 37 34 34 37 37 38 38 3b 3b
  //   3d 3d 3a 3b 40 3 6 3 c 45 7 45 18 9 b 9 c 4f a 4f d0 d1 13 d1 14 57 12 57 18 5b 1e 5b 14 5d 1f 5d 40
  //   61 23 61 24 27 22 27 28 6b 2e 6b 24 2d 2f 2d 70 33 36 33 3c 35 37 35 28 39 3b 39 3c 3f 3a 3f 41 41 6
  //   7 44 44 7 7 8 8 b 4b d d a 4b d0 d0 13 53 15 15 12 53 19 19 1e 5f 5c 5c 1f 5f 60 60 23 23 25 25 22
  //   23 29 29 2e 6f 2c 2c 2f 6f 71 71 36 37 34 34 37 37 38 38 3b 3b 3d 3d 3a 3b 40 3 6 3 c 45 7 45 18 9 b
  //   9 c 4f a 4f d0 d1 13 d1 14 57 12 57 18 5b 1e 5b 14 5d 1f 5d 60 61 23 61 24 27 22 27 28 6b 2e 6b 24
  //   2d 2f 2d 70 33 36 33 3c 35 37 35 28 39 3b 39 3c 3f 3a 3f 40 41 6 7 44 44 7 7 8 8 b 4b d d a 4b d0 d0
  //   13 53 15 15 12 53 19 19 1e 5f 5c 5c 1f 5f 60 60 23 23 25 25 22 23 29 29 2e 6f 2c 2c 2f 6f 71 71 36
  //   37 34 34 37 37 38 38 3b 3b 3d 3d 3a 3b 40 3 6 3 c 45 7 45 18 9 b 9 c 4f a 4f d0 d1 13 d1 14 57 12 57
  //   18 5b 1e 5b 14 5d 1f 5d 40 61 23 61 24 27 22 27 28 6b 2e 6b 24 2d 2f 2d 70 33 36 33 3c 35 37 35 28
  //   39 3b 39 3c 3f 3a 3f 41 41 6 7 44 44 7 7 8 8 b 4b d d a 4b d0 d0 13 53 15 15 12 53 19 19 1e 5f 5c 5c
  //   1f 5f 60 60 23 23 25 25 22 23 29 29 2e 6f 2c 2c 2f 6f 71 71 36 37 34 34 37 37 38 38 3b 3b 3d 3d 3a
  //   3b 40 3 6 3 c 45 7 45 18 9 b 9 c 4f a 4f d0 d1 13 d1 14 57 12 57 18 5b 1e 5b 14 5d 1f 5d 60 61 23 61
  //   24 27 22 27 28 6b 2e 6b 24 2d 2f 2d 70 33 36 33 3c 35 37 35 28 39 3b 39 3c 3f 3a 3f 40 41 6 7 4 4 7
  //   7 8 8 b 4b d d a 4b d0 d0 13 53 15 15 12 53 59 59 1e 5f 5c 5c 1f 5f 60 60 23 23 25 25 22 23 29 29 2e
  //   6f 2c 2c 2f 6f 71 71 36 37 34 34 37 37 38 38 3b 3b 3d 3d 3a 3b 40 3 6 3 c 5 7 5 58 9 b 9 c 4f a 4f
  //   d0 d1 13 d1 14 57 12 57 58 5b 1e 5b 14 5d 1f 5d 40 61 23 61 24 27 22 27 28 6b 2e 6b 24 2d 2f 2d 70
  //   33 36 33 3c 35 37 35 28 39 3b 39 3c 3f 3a 3f 41 41 6 7 4 4 7 7 8 8 b 4b d d a 4b d0 d0 13 53 15 15
  //   12 53 59 59 1e 5f 5c 5c 1f 5f 60 60 23 23 25 25 22 23 29 29 2e 6f 2c 2c 2f 6f 71 71 36 37 34 34 37
  //   37 38 38 3b 3b 3d 3d 3a 3b 40 3 6 3 c 5 7 5 58 9 b 9 c 4f a 4f d0 d1 13 d1 14 57 12 57 58 5b 1e 5b
  //   14 5d 1f 5d 60 61 23 61 24 27 22 27 28 6b 2e 6b 24 2d 2f 2d 70 33 36 33 3c 35 37 35 28 39 3b 39 3c
  //   3f 3a 3f 40 41 6 7 4 4 7 7 8 8 b 4b d d a 4b d0 d0 13 53 15 15 12 53 59 59 1e 5f 5c 5c 1f 5f 60 60
  //   23 23 25 25 22 23 29 29 2e 6f 2c 2c 2f 6f 71 71 36 37 34 34 37 37 38 38 3b 3b 3d 3d 3a 3b 40 3 6 3 c
  //   5 7 5 58 9 b 9 c 4f a 4f d0 d1 13 d1 14 57 12 57 58 5b 1e 5b 14 5d 1f 5d 40 61 23 61 24 27 22 27 28
  //   6b 2e 6b 24 2d 2f 2d 70 33 36 33 3c 35 37 35 28 39 3b 39 3c 3f 3a 3f 41 41 6 7 4 4 7 7 8 8 b 4b d d
  //   a 4b d0 d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
endmodule

module morse_transmitter (
  input  clk,
  input  char_available,
  input  [7:0] parallel_in,
  input  rst,
  output load_next_char,
  output serial_out
);

  wire and_1_out, bit_ready, buffer_1_out, buffer_2_out, buffer_3_out, buffer_4_out, buffer_5_out,
       buffer_6_out, buffer_7_out, buffer_8_out, buffer_10_out, buffer_11_out, buffer_12_out, buffer_13_out,
       buffer_14_out, buffer_15_out, buffer_16_out, buffer_17_out, buffer_18_out, buffer_19_out,
       buffer_20_out, buffer_21_out, buffer_22_out, buffer_23_out, buffer_24_out, buffer_25_out,
       counter_1_carry, counter_2_carry, counter_3_carry, counter_4_carry, counter_5_carry, dash, dot,
       not_1_out, not_2_out, or_1_out, shift_bits, shift_register_1_q0, shift_register_1_q1,
       shift_register_1_q2, shift_register_1_q3, shift_register_1_q4, shift_register_1_q5,
       shift_register_1_q6, shifter_empty, shifter_not_empty, space, transmitter_idle;
  wire [0:0] shift_register_1_out;
  wire [7:0] Morse_Codes_data;

  ROM Morse_Codes (.addr(parallel_in), .data(Morse_Codes_data));
  buf buffer_1 (buffer_1_out, shifter_empty);
  buf buffer_2 (buffer_2_out, buffer_5_out);
  buf buffer_3 (buffer_3_out, buffer_2_out);
  buf buffer_4 (buffer_4_out, buffer_3_out);
  buf buffer_5 (buffer_5_out, buffer_1_out);
  or or_1 (or_1_out, shift_bits, load_next_char);
  buf buffer_6 (buffer_6_out, buffer_7_out);
  buf buffer_7 (buffer_7_out, buffer_17_out);
  buf buffer_8 (buffer_8_out, buffer_6_out);
  buf buffer_9 (bit_ready, buffer_8_out);
  buf buffer_10 (buffer_10_out, buffer_4_out);
  buf buffer_11 (buffer_11_out, buffer_10_out);
  buf buffer_12 (buffer_12_out, buffer_11_out);
  buf buffer_13 (buffer_13_out, buffer_12_out);
  buf buffer_14 (buffer_14_out, char_available);
  buf buffer_15 (buffer_15_out, buffer_14_out);
  buf buffer_16 (buffer_16_out, buffer_15_out);
  not not_1 (not_1_out, or_1_out);
  and and_1 (and_1_out, not_1_out, or_1_out);
  buf buffer_17 (buffer_17_out, buffer_18_out);
  buf buffer_18 (buffer_18_out, and_1_out);
  buf buffer_19 (buffer_19_out, buffer_13_out);
  buf buffer_20 (buffer_20_out, buffer_19_out);
  buf buffer_21 (buffer_21_out, buffer_20_out);
  buf buffer_22 (buffer_22_out, buffer_21_out);
  buf buffer_23 (buffer_23_out, buffer_16_out);
  buf buffer_24 (buffer_24_out, buffer_23_out);
  buf buffer_25 (buffer_25_out, buffer_24_out);
  and and_2 (shift_bits, shifter_not_empty, transmitter_idle);
  // Probe on Morse_Codes_data
  not not_2 (not_2_out, shifter_not_empty);
  Shift_Register shift_register_1 (
    .shift(shifter_not_empty), .in(1'b0), .clk(and_1_out), .out(shift_register_1_out[0]), .load(not_2_out),
    .clr(rst), .d0(Morse_Codes_data[7]), .q0(shift_register_1_q0), .d1(Morse_Codes_data[6]),
    .q1(shift_register_1_q1), .d2(Morse_Codes_data[5]), .q2(shift_register_1_q2), .d3(Morse_Codes_data[4]),
    .q3(shift_register_1_q3), .d4(Morse_Codes_data[3]), .q4(shift_register_1_q4), .d5(Morse_Codes_data[2]),
    .q5(shift_register_1_q5), .d6(Morse_Codes_data[1]), .q6(shift_register_1_q6), .d7(Morse_Codes_data[0]));  // open: q7
  not not_3 (shifter_empty, shifter_not_empty);
  and and_3 (load_next_char, buffer_22_out, buffer_25_out, transmitter_idle);
  or or_2 (shifter_not_empty, shift_register_1_q0, shift_register_1_q1, shift_register_1_q2, shift_register_1_q3, shift_register_1_q4, shift_register_1_q5, shift_register_1_q6);
  Demultiplexer #(.enable("false"), .select(2)) demultiplexer_1 (
    .out1(space), .out2(dot), .out3(dash), .in(bit_ready), .sel({shifter_not_empty, shift_register_1_out[0]}));  // open: out0
  Counter #(.max('h3), .ongoal("stay")) counter_1 (
    .load(rst), .D(8'h3), .carry(counter_1_carry), .clk(clk), .clr(dot));  // open: count, Q, up
  Counter #(.max('hb), .ongoal("stay")) counter_2 (
    .load(rst), .D(8'hb), .carry(counter_2_carry), .clk(clk), .clr(dash));  // open: count, Q, up
  Counter #(.max('hb), .ongoal("stay")) counter_3 (
    .load(rst), .D(8'hb), .carry(counter_3_carry), .clk(clk), .clr(space));  // open: count, Q, up
  Counter #(.max('h3), .ongoal("stay")) counter_4 (
    .load(rst), .D(8'h3), .count(counter_1_carry), .carry(counter_4_carry), .clk(clk), .clr(dot));  // open: Q, up
  Counter #(.max('h3), .ongoal("stay")) counter_5 (
    .load(rst), .D(8'h3), .count(counter_2_carry), .carry(counter_5_carry), .clk(clk), .clr(dash));  // open: Q, up
  or or_3 (serial_out, ~counter_1_carry, ~counter_2_carry);  // OR_Gate
  and and_4 (transmitter_idle, counter_4_carry, counter_5_carry, counter_3_carry);

  // Notes on the sheet:
  //   contents of Morse_Codes (hex, n*v repeats v):
  //   32*0 1 67 52 0 0 0 22 5e 2d 6d 0 2a 73 61 6a 29 3f 3e 3c 38 30 20 21 23 27 2f 47 35 0 31 0 4c 56 6
  //   11 15 9 2 14 b 10 4 1e d 12 7 5 f 16 1b a 8 3 c 18 e 19 1d 13 0 39 0 0 6c 0 6 11 15 9 2 14 b 10 4 1e
  //   d 12 7 5 f 16 1b a 8 3 c 18 e 19 1d 13 69*0 36 0 0 0 1a 0 0 0 32 24 6*0 2c 5*0 17 5*0 1c 0 0 0 36 0
  //   0 0 1a 0 0 0 32 24 6*0 2c 5*0 17 5*0 1c
endmodule

module morse_receiver (
  input  rst,
  input  clk,
  input  morse_in,
  output [7:0] parallel_out,
  output data_ready,
  output [3:0] diagnostic_out
);

  wire and_1_out, and_2_out, buffer_1_out, buffer_2_out, buffer_3_out, buffer_4_out, buffer_5_out,
       buffer_6_out, buffer_7_out, buffer_8_out, buffer_9_out, buffer_10_out, buffer_11_out, buffer_12_out,
       buffer_13_out, buffer_14_out, buffer_15_out, buffer_16_out, buffer_17_out, buffer_18_out,
       buffer_19_out, buffer_20_out, buffer_21_out, buffer_22_out, buffer_23_out, buffer_24_out,
       buffer_25_out, buffer_26_out, buffer_27_out, buffer_28_out, nor_1_out, nor_2_out, not_1_out,
       not_2_out, not_3_out, not_4_out, not_5_out, not_6_out, or_1_out, shift_register_1_out;
  wire [6:0] shift_register_1_q0;

  Counter #(.max('h6), .ongoal("stay"), .width(3)) counter_1 (
    .load(rst), .D(3'b110), .carry(diagnostic_out[1]), .clk(clk), .clr(morse_in));  // open: count, Q, up
  Counter #(.max('h8), .ongoal("stay"), .width(4)) counter_2 (
    .load(rst), .D(4'b1000), .count(diagnostic_out[1]), .carry(diagnostic_out[0]), .clk(clk), .clr(morse_in));  // open: Q, up
  Counter #(.max('h5), .ongoal("stay"), .width(3)) counter_3 (
    .carry(diagnostic_out[2]), .clk(clk), .clr(not_1_out));  // open: load, D, count, Q, up
  not not_1 (not_1_out, morse_in);
  not not_2 (not_2_out, diagnostic_out[0]);
  not not_3 (not_3_out, diagnostic_out[1]);
  buf buffer_1 (buffer_1_out, diagnostic_out[2]);
  buf buffer_2 (buffer_2_out, buffer_1_out);
  buf buffer_3 (buffer_3_out, buffer_2_out);
  not not_4 (not_4_out, diagnostic_out[1]);
  buf buffer_4 (buffer_4_out, diagnostic_out[1]);
  buf buffer_5 (buffer_5_out, buffer_4_out);
  and and_1 (and_1_out, not_2_out, diagnostic_out[0]);
  buf buffer_6 (buffer_6_out, and_1_out);
  and and_2 (and_2_out, not_3_out, diagnostic_out[1]);
  buf buffer_7 (buffer_7_out, buffer_3_out);
  buf buffer_8 (buffer_8_out, buffer_7_out);
  buf buffer_9 (buffer_9_out, buffer_8_out);
  nor nor_1 (nor_1_out, morse_in, not_5_out);
  not not_5 (not_5_out, morse_in);
  nor nor_2 (nor_2_out, not_4_out, diagnostic_out[1]);
  buf buffer_10 (buffer_10_out, buffer_5_out);
  buf buffer_11 (buffer_11_out, buffer_10_out);
  buf buffer_12 (buffer_12_out, buffer_11_out);
  buf buffer_13 (buffer_13_out, buffer_6_out);
  buf buffer_14 (buffer_14_out, buffer_13_out);
  buf buffer_15 (buffer_15_out, buffer_14_out);
  buf buffer_16 (buffer_16_out, buffer_15_out);
  or or_1 (or_1_out, nor_1_out, nor_2_out, and_1_out);
  buf buffer_17 (buffer_17_out, buffer_12_out);
  buf buffer_18 (buffer_18_out, buffer_16_out);
  buf buffer_19 (buffer_19_out, buffer_18_out);
  buf buffer_20 (buffer_20_out, buffer_19_out);
  buf buffer_21 (buffer_21_out, buffer_20_out);
  not not_6 (not_6_out, buffer_17_out);
  Shift_Register shift_register_1 (
    .shift(not_6_out), .in(buffer_9_out), .clk(or_1_out), .out(shift_register_1_out), .load(buffer_17_out),
    .clr(rst), .d0(1'b1), .q0(shift_register_1_q0[0]), .d1(1'b0), .q1(shift_register_1_q0[1]), .d2(1'b0),
    .q2(shift_register_1_q0[2]), .d3(1'b0), .q3(shift_register_1_q0[3]), .d4(1'b0),
    .q4(shift_register_1_q0[4]), .d5(1'b0), .q5(shift_register_1_q0[5]), .d6(1'b0),
    .q6(shift_register_1_q0[6]), .d7(1'b0), .q7(shift_register_1_out));
  buf buffer_22 (buffer_22_out, buffer_21_out);
  buf buffer_23 (buffer_23_out, buffer_22_out);
  buf buffer_24 (buffer_24_out, buffer_23_out);
  buf buffer_25 (buffer_25_out, buffer_24_out);
  ROM #(.addrWidth(7)) rom_1 (.addr(shift_register_1_q0), .data(parallel_out));
  buf buffer_26 (buffer_26_out, buffer_25_out);
  buf buffer_27 (buffer_27_out, buffer_26_out);
  buf buffer_28 (buffer_28_out, buffer_27_out);
  or or_2 (data_ready, buffer_28_out, and_2_out);

  assign diagnostic_out[3] = morse_in;

  // Notes on the sheet:
  //   contents of rom_1 (hex, n*v repeats v):
  //   0 20 65 74 69 61 6e 6d 73 75 72 77 64 6b 67 6f 68 76 66 fc 6c e4 70 6a 62 78 63 79 7a 71 f6 20 35 34
  //   0 33 e9 0 f0 32 26 e8 2b 0 0 e0 0 31 36 3d 2f 5c 0 3b 28 0 37 20 0 0 38 0 39 30 12*0 3f 5f 4*0 22 0
  //   0 2e 4*0 40 0 0 0 27 0 0 2d 11*0 29 5*0 2c 4*0 3a 21 d1 a8 9d d2 25 31
endmodule

module uart_receiver (
  input  rst,
  input  clk,
  input  serial_in,
  output [7:0] data_out,
  output data_ready,
  output framing_error,
  output parity_error
);

  wire and_1_out, bitselector_1_out, counter_1_carry, odd_parity_1_out, or_1_out, shift_register_1_out,
       shift_register_1_q0, shift_register_1_q1, xor_1_out;
  wire [7:0] counter_1_q;

  and and_1 (and_1_out, ~serial_in, counter_1_carry);  // AND_Gate
  BitSelector bitselector_1 (.in(counter_1_q), .out(bitselector_1_out), .sel(3'b001));
  Counter #(.max('h2c), .ongoal("stay")) counter_1 (
    .load(rst), .D(8'h2c), .Q(counter_1_q), .carry(counter_1_carry), .clk(clk), .clr(and_1_out));  // open: count, up
  Shift_Register #(.length(11)) shift_register_1 (
    .in(serial_in), .clk(bitselector_1_out), .out(shift_register_1_out), .clr(rst), .q0(shift_register_1_q0),
    .q1(shift_register_1_q1), .q2(data_out[7]), .q3(data_out[6]), .q4(data_out[5]), .q5(data_out[4]),
    .q6(data_out[3]), .q7(data_out[2]), .q8(data_out[1]), .q9(data_out[0]));  // open: shift, load, d0, d1, d2, d3, d4, d5, d6, d7, d8, d9, d10, q10
  xor odd_parity_1 (odd_parity_1_out, data_out[0], data_out[1], data_out[2], data_out[3], data_out[4], data_out[5], data_out[6], data_out[7]);
  ExactlyOne xor_1 (.out(xor_1_out), .in0(1'b1), .in1(shift_register_1_q1), .in2(odd_parity_1_out));
  or or_1 (or_1_out, ~shift_register_1_q0, shift_register_1_out);  // OR_Gate
  and and_2 (framing_error, counter_1_carry, or_1_out);
  and and_3 (parity_error, counter_1_carry, xor_1_out);
  and and_4 (data_ready, counter_1_carry, ~framing_error, ~parity_error);  // AND_Gate
endmodule

module uart_transmitter (
  input  rst,
  input  clk,
  input  input_availlable,
  input  [7:0] parallel_in,
  output next_input,
  output serial_out
);

  wire and_1_out, buffer_1_out, buffer_2_out, buffer_3_out, buffer_4_out, buffer_5_out, buffer_7_out,
       buffer_8_out, buffer_10_out, buffer_11_out, j_k_ff_1_q, j_k_ff_1_qn, load, not_1_out,
       odd_parity_1_out, or_1_out, or_2_out, set_load, shift, shift_register_1_out, start_transmission,
       transmitter_idle, xor_1_out;
  wire [7:0] counter_1_q;

  Counter #(.max('h30), .ongoal("stay")) counter_1 (
    .load(rst), .D(8'h30), .Q(counter_1_q), .carry(transmitter_idle), .clk(clk), .clr(start_transmission));  // open: count, up
  BitSelector bitselector_1 (.in(counter_1_q), .out(shift), .sel(3'b001));
  J_K_Flip_Flop j_k_ff_1 (.Q(j_k_ff_1_q), .Qn(j_k_ff_1_qn), .preset(next_input), .reset(or_1_out));  // open: J, clk, K
  or or_1 (or_1_out, set_load, rst);
  or or_2 (or_2_out, load, shift);
  not not_1 (not_1_out, and_1_out);
  and and_1 (and_1_out, input_availlable, transmitter_idle);
  xor odd_parity_1 (odd_parity_1_out, parallel_in[0], parallel_in[1], parallel_in[2], parallel_in[3], parallel_in[4], parallel_in[5], parallel_in[6], parallel_in[7]);
  xor xor_1 (xor_1_out, 1'b1, odd_parity_1_out);
  Shift_Register #(.length(12)) shift_register_1 (
    .shift(j_k_ff_1_q), .in(1'b1), .clk(or_2_out), .out(shift_register_1_out), .load(j_k_ff_1_qn), .clr(rst),
    .d0(1'b1), .d1(xor_1_out), .d2(parallel_in[7]), .d3(parallel_in[6]), .d4(parallel_in[5]),
    .d5(parallel_in[4]), .d6(parallel_in[3]), .d7(parallel_in[2]), .d8(parallel_in[1]), .d9(parallel_in[0]),
    .d10(1'b0), .d11(1'b1));  // open: q0, q1, q2, q3, q4, q5, q6, q7, q8, q9, q10, q11
  and and_2 (set_load, not_1_out, and_1_out);
  buf buffer_1 (buffer_1_out, set_load);
  buf buffer_2 (buffer_2_out, buffer_1_out);
  buf buffer_3 (buffer_3_out, buffer_2_out);
  buf buffer_4 (buffer_4_out, buffer_3_out);
  buf buffer_5 (buffer_5_out, buffer_4_out);
  buf buffer_6 (load, buffer_5_out);
  buf buffer_7 (buffer_7_out, load);
  or or_3 (serial_out, shift_register_1_out, transmitter_idle);
  buf buffer_8 (buffer_8_out, buffer_7_out);
  buf buffer_9 (next_input, buffer_8_out);
  buf buffer_10 (buffer_10_out, next_input);
  buf buffer_11 (buffer_11_out, buffer_10_out);
  buf buffer_12 (start_transmission, buffer_11_out);

  // Other names for the same wires on the sheet: input_available = input_availlable; set_shift = next_input
endmodule

module EPROM_morse_transmitter (
  input  clk,
  input  char_available,
  input  [7:0] parallel_in,
  input  rst,
  output load_next_char,
  output serial_out
);

  wire buffer_1_out, buffer_2_out, buffer_3_out, buffer_4_out, buffer_5_out, buffer_6_out, counter_1_carry,
       not_OE_out, or_1_out, transmitter_idle;
  wire [6:0] MORSE_ROM_STATE_MACHINE_data, multiplexer_1_out;
  wire [7:0] MORSE_ROM_ASCII_LOOKUP_data;
  wire [7:7] MORSE_ROM_STATE_MACHINE_data_2, t_ff_1_q;

  ROM #(.addrWidth(9)) MORSE_ROM_ASCII_LOOKUP (.addr({1'b1, parallel_in}), .data(MORSE_ROM_ASCII_LOOKUP_data));
  buf buffer_1 (buffer_1_out, char_available);
  buf buffer_2 (buffer_2_out, buffer_1_out);
  buf buffer_3 (buffer_3_out, buffer_2_out);
  buf buffer_4 (buffer_4_out, buffer_3_out);
  buf buffer_5 (buffer_5_out, buffer_4_out);
  buf buffer_6 (buffer_6_out, buffer_5_out);
  // Probe on MORSE_ROM_ASCII_LOOKUP_data[6:0]
  and and_1 (load_next_char, buffer_6_out, transmitter_idle);
  Multiplexer #(.enable("false"), .width(7)) multiplexer_1 (
    .in0(MORSE_ROM_STATE_MACHINE_data), .in1(MORSE_ROM_ASCII_LOOKUP_data[6:0]), .out(multiplexer_1_out),
    .sel(or_1_out));
  Counter #(.max('h3), .width(2)) counter_1 (
    .carry(counter_1_carry), .clk(clk), .clr(or_1_out));  // open: load, D, count, Q, up
  or or_1 (or_1_out, rst, load_next_char);
  // Probe on MORSE_ROM_STATE_MACHINE_data
  ROM #(.addrWidth(9)) MORSE_ROM_STATE_MACHINE (
    .addr({1'b0, t_ff_1_q[7], multiplexer_1_out}),
    .data({MORSE_ROM_STATE_MACHINE_data_2[7], MORSE_ROM_STATE_MACHINE_data}));
  T_Flip_Flop #(.trigger("falling")) t_ff_1 (
    .clk(counter_1_carry), .T(1'b1), .Q(t_ff_1_q[7]), .reset(or_1_out));  // open: Qn, preset
  Pull_Resistor pull_resistor_1 (.node(serial_out));
  assign serial_out = not_OE_out ? MORSE_ROM_STATE_MACHINE_data_2[7] : 1'bz;  // Controlled_Buffer controlled_buffer_1
  not not_OE (not_OE_out, or_1_out);
  nor nor_1 (transmitter_idle, MORSE_ROM_STATE_MACHINE_data[0], MORSE_ROM_STATE_MACHINE_data[1], MORSE_ROM_STATE_MACHINE_data[2], MORSE_ROM_STATE_MACHINE_data[3], MORSE_ROM_STATE_MACHINE_data[4], MORSE_ROM_STATE_MACHINE_data[5], MORSE_ROM_STATE_MACHINE_data[6]);

  // Notes on the sheet:
  //   contents of MORSE_ROM_ASCII_LOOKUP (hex, n*v repeats v):
  //   0 89 86 83 85 85 86 83 0 89 8a 8a 8c 9d 9e 8f 94 91 92 92 94 b5 86 97 98 89 98 9b 98 9d 9e 9b a1 a1
  //   a2 b3 a4 85 a4 27 a8 ad ae ab 8c ad ae 8f b0 a1 b0 b3 a4 b5 b6 b6 bc b9 ba ab bc ad ae bf 40 c1 c2
  //   c2 c4 c1 c4 c7 48 48 da cb cd cd ce cb d0 d0 d0 d3 c4 d5 d6 d3 d9 d9 da da dc d9 dc df e0 e5 c2 e3
  //   e0 e5 e6 67 e9 e9 ea e3 ec cd ce ef f1 f1 f2 f1 f4 f4 f2 f7 f8 fd f8 fb ec fd fe ef 0 81 2 43 4 45
  //   46 87 8 49 ca b cc d 8e cf 10 d1 52 93 d4 95 96 57 58 19 1a 5b 9c dd 5e 9f a0 61 e2 23 64 a5 26 27
  //   68 a9 aa 6b 2c 6d 6e 2f 70 31 b2 f3 b4 75 76 b7 38 f9 fa bb fc 3d 3e ff 40 81 2 43 4 45 46 87 8 49
  //   ca b cc d 8e cf 10 d1 52 93 d4 95 96 57 58 19 1a 5b 9c dd 5e 9f a0 61 e2 23 64 a5 26 67 68 a9 aa 6b
  //   2c 6d 6e 2f 70 31 b2 f3 b4 75 76 b7 38 f9 fa bb fc 3d 3e ff 32*0 48 7b 0 0 53 0 4b 0 0 0 12 28 77 47
  //   17 39 55 35 66 30 42 1b 5f f 6a 3a 3f 0 0 22 0 7e 0 5 a 69 5c 9 2d c 5a 59 24 14 1e 65 1d 60 6c 11
  //   4d 18 41 44 6 21 56 33 4e 2b 72 36 0 0 0 5 a 69 5c 9 2d c 5a 59 24 14 1e 65 1d 60 6c 11 4d 18 41 44
  //   6 21 56 33 4e 3 0 6f 50*0 63 19*0 50 17*0 3c 5*0 71 0 2e 5*0 50 17*0 3c 5*0 71 0 2e
  //   contents of MORSE_ROM_STATE_MACHINE (hex, n*v repeats v):
  //   0 89 86 83 85 85 86 83 0 89 8a 8a 8c 9d 9e 8f 94 91 92 92 94 b5 86 97 98 89 98 9b 98 9d 9e 9b a1 a1
  //   a2 b3 a4 85 a4 27 a8 ad ae ab 8c ad ae 8f b0 a1 b0 b3 a4 b5 b6 b6 bc b9 ba ab bc ad ae bf 40 c1 c2
  //   c2 c4 c1 c4 c7 48 48 da cb cd cd ce cb d0 d0 d0 d3 c4 d5 d6 d3 d9 d9 da da dc d9 dc df e0 e5 c2 e3
  //   e0 e5 e6 67 e9 e9 ea e3 ec cd ce ef f1 f1 f2 f1 f4 f4 f2 f7 f8 fd f8 fb ec fd fe ef 0 81 2 43 4 45
  //   46 87 8 49 ca b cc d 8e cf 10 d1 52 93 d4 95 96 57 58 19 1a 5b 9c dd 5e 9f a0 61 e2 23 64 a5 26 27
  //   68 a9 aa 6b 2c 6d 6e 2f 70 31 b2 f3 b4 75 76 b7 38 f9 fa bb fc 3d 3e ff 40 81 2 43 4 45 46 87 8 49
  //   ca b cc d 8e cf 10 d1 52 93 d4 95 96 57 58 19 1a 5b 9c dd 5e 9f a0 61 e2 23 64 a5 26 67 68 a9 aa 6b
  //   2c 6d 6e 2f 70 31 b2 f3 b4 75 76 b7 38 f9 fa bb fc 3d 3e ff 32*0 48 7b 0 0 53 0 4b 0 0 0 12 28 77 47
  //   17 39 55 35 66 30 42 1b 5f f 6a 3a 3f 0 0 22 0 7e 0 5 a 69 5c 9 2d c 5a 59 24 14 1e 65 1d 60 6c 11
  //   4d 18 41 44 6 21 56 33 4e 2b 72 36 0 0 0 5 a 69 5c 9 2d c 5a 59 24 14 1e 65 1d 60 6c 11 4d 18 41 44
  //   6 21 56 33 4e 3 0 6f 50*0 63 19*0 50 17*0 3c 5*0 71 0 2e 5*0 50 17*0 3c 5*0 71 0 2e
endmodule
